# Fritzing sketch Drona1 (saved by Fritzing 0.9.3b)
breadboards: 1

parts:
  IC1 = IC, DIP package, 16 pins [chip_label=L293D]
  IC3 = IC, DIP package, 16 pins [chip_label=L293D]
  Part2 = Arduino Uno (Rev3) - ICSP
  M1 = DC Motor
  M2 = DC Motor
  M3 = DC Motor
  U1 = LIPO-1000mAh [package=lipo-1000]
  U2 = LIPO-1000mAh [package=lipo-1000]

nets:
  N1: IC1.pin1, Part2.ICSP_MOSI, Part2.D11_PWM/MOSI
  N2: IC1.pin2, Part2.D7
  N3: IC1.pin3, M1.pin_2
  N4: IC1.pin4, IC3.pin4, IC3.pin12, Part2.GND, U1.-, U2.-
  N5: IC1.pin6, M1.pin_1
  N6: IC1.pin7, Part2.D6_PWM
  N7: IC1.pin8, U1.+
  N8: IC1.pin16, IC3.pin16, Part2.5V
  N9: IC3.pin1, Part2.D9_PWM
  N10: IC3.pin2, Part2.D3_PWM
  N11: IC3.pin3, M3.pin_2
  N12: IC3.pin6, M3.pin_1
  N13: IC3.pin7, Part2.D2
  N14: IC3.pin8, U2.+
  N15: IC3.pin9, Part2.D10_PWM/SS
  N16: IC3.pin10, Part2.D4
  N17: IC3.pin11, M2.pin_2
  N18: IC3.pin14, M2.pin_1
  N19: IC3.pin15, Part2.D5_PWM
